// Logisim project TallerLogica-Combinatorios.circ as structural Verilog: 12 circuits, main circuit sumador_simple
module sumador_simple (
  input  A,
  input  B,
  output S,
  output Cout
);

  xor xor_1 (S, A, B);
  and and_1 (Cout, A, B);
endmodule

module sumador_completo (
  input  A,
  input  B,
  input  Cin,
  output S,
  output Cout
);

  wire sumador_simple_1_cout, sumador_simple_1_s, sumador_simple_2_cout;

  sumador_simple sumador_simple_1 (.A(A), .B(B), .S(sumador_simple_1_s), .Cout(sumador_simple_1_cout));
  sumador_simple sumador_simple_2 (.A(sumador_simple_1_s), .B(Cin), .S(S), .Cout(sumador_simple_2_cout));
  or or_1 (Cout, sumador_simple_1_cout, sumador_simple_2_cout);
endmodule

module sumador_4 (
  input  [3:0] A,
  input  Cin,
  input  [3:0] B,
  output [3:0] S,
  output Cout
);

  wire sumador_completo_1_cout, sumador_completo_2_cout, sumador_completo_3_cout;

  sumador_completo sumador_completo_1 (.A(A[0]), .B(B[0]), .Cin(Cin), .S(S[0]), .Cout(sumador_completo_1_cout));
  sumador_completo sumador_completo_2 (
    .A(A[1]), .B(B[1]), .Cin(sumador_completo_1_cout), .S(S[1]), .Cout(sumador_completo_2_cout));
  sumador_completo sumador_completo_3 (
    .A(A[2]), .B(B[2]), .Cin(sumador_completo_2_cout), .S(S[2]), .Cout(sumador_completo_3_cout));
  sumador_completo sumador_completo_4 (.A(A[3]), .B(B[3]), .Cin(sumador_completo_3_cout), .S(S[3]), .Cout(Cout));
  Hex_Digit_Display hex_digit_display_1 (.value(S));  // open: dp
endmodule

module comparador_cero (
  input  [3:0] A,
  output Z
);

  wire nor_1_out, nor_2_out;

  nor nor_1 (nor_1_out, A[0], A[1]);
  nor nor_2 (nor_2_out, A[2], A[3]);
  and and_1 (Z, nor_1_out, nor_2_out);
endmodule

module sumador_flags (
  input  [3:0] A,
  input  Cin,
  input  [3:0] B,
  output [3:0] S,
  output N,
  output V,
  output Z,
  output C
);

  wire not_1_out, OverNeg0_out, OverNeg2_out, OverPos0_out, OverPos1_out;

  sumador_4 sumador_4_1 (.A(A), .Cin(Cin), .B(B), .S({N, S[2:0]}), .Cout(C));
  and OverNeg0 (OverNeg0_out, A[3], B[3]);
  nor OverPos0 (OverPos0_out, A[3], B[3]);
  comparador_cero comparador_cero_1 (.A({N, S[2:0]}), .Z(Z));
  Hex_Digit_Display hex_digit_display_1 (.value({N, S[2:0]}));  // open: dp
  not not_1 (not_1_out, N);
  and OverNeg2 (OverNeg2_out, not_1_out, OverNeg0_out);
  and OverPos1 (OverPos1_out, N, OverPos0_out);
  or or_1 (V, OverNeg2_out, OverPos1_out);

  assign S[3] = N;
endmodule

module incrementador_4 (
  input  [3:0] A,
  output [3:0] S
);

  sumador_4 sumador_4_1 (.A(4'b0001), .B(A), .S(S));  // open: Cin, Cout
  Hex_Digit_Display hex_digit_display_1 (.value(S));  // open: dp

  // Notes on the sheet:
  //   Unidad
endmodule

module inversor_4 (
  input  [3:0] A,
  input  INV,
  output [3:0] S
);

  wire [3:0] incrementador_4_1_s, xor_1_out;

  xor xor_1 (xor_1_out[0], A[0], INV);
  xor xor_2 (xor_1_out[1], A[1], INV);
  xor xor_3 (xor_1_out[2], A[2], INV);
  xor xor_4 (xor_1_out[3], A[3], INV);
  Multiplexer #(.width(4)) multiplexer_1 (.in0(A), .in1(incrementador_4_1_s), .out(S), .sel(INV));
  incrementador_4 incrementador_4_1 (.A(xor_1_out), .S(incrementador_4_1_s));
  Hex_Digit_Display hex_digit_display_1 (.value(S));  // open: dp
endmodule

module ALU (
  input  [3:0] A,
  input  [3:0] B,
  input  [1:0] OP,
  output N,
  output V,
  output Z,
  output [3:0] S,
  output C
);

  wire andbitabit_1_n, andbitabit_1_z, comparador_cero_1_z, es1000_1_out_2, multiplexer_5_out, not_1_out,
       or_1_out, orbitabit_1_n, orbitabit_1_z, sumador_flags_1_c, sumador_flags_1_n, sumador_flags_1_v,
       sumador_flags_1_z, sumador_flags_2_c, sumador_flags_2_n, sumador_flags_2_v, sumador_flags_2_z,
       xnor_1_out;
  wire [3:0] andbitabit_1_s, inversor_4_1_s, orbitabit_1_s, sumador_flags_1_s, sumador_flags_2_s;

  ANDBitaBit andbitabit_1 (.A(A), .B(B), .Z(andbitabit_1_z), .S(andbitabit_1_s), .N(andbitabit_1_n));
  ORBitABit orbitabit_1 (.A(A), .B(B), .Z(orbitabit_1_z), .S(orbitabit_1_s), .N(orbitabit_1_n));
  inversor_4 inversor_4_1 (.A(B), .INV(1'b1), .S(inversor_4_1_s));
  sumador_flags sumador_flags_1 (
    .A(A), .B(B), .S(sumador_flags_1_s), .N(sumador_flags_1_n), .V(sumador_flags_1_v), .Z(sumador_flags_1_z),
    .C(sumador_flags_1_c));  // open: Cin
  sumador_flags sumador_flags_2 (
    .A(A), .B(inversor_4_1_s), .S(sumador_flags_2_s), .N(sumador_flags_2_n), .V(sumador_flags_2_v),
    .Z(sumador_flags_2_z), .C(sumador_flags_2_c));  // open: Cin
  or or_1 (or_1_out, sumador_flags_2_v, es1000_1_out_2);
  not not_1 (not_1_out, sumador_flags_2_c);
  Multiplexer #(.select(2), .width(4)) multiplexer_1 (
    .in0(sumador_flags_1_s), .in1(sumador_flags_2_s), .in2(andbitabit_1_s), .in3(orbitabit_1_s), .out(S),
    .sel(OP));
  Multiplexer #(.select(2)) multiplexer_2 (
    .in0(sumador_flags_1_n), .in1(sumador_flags_2_n), .in2(andbitabit_1_n), .in3(orbitabit_1_n), .out(N),
    .sel(OP));
  Multiplexer #(.select(2)) multiplexer_3 (
    .in0(sumador_flags_1_v), .in1(or_1_out), .in2(1'b0), .in3(1'b0), .out(V), .sel(OP));
  Multiplexer #(.select(2)) multiplexer_4 (
    .in0(sumador_flags_1_z), .in1(sumador_flags_2_z), .in2(andbitabit_1_z), .in3(orbitabit_1_z), .out(Z),
    .sel(OP));
  Multiplexer #(.select(2)) multiplexer_5 (
    .in0(sumador_flags_1_c), .in1(not_1_out), .in2(1'b0), .in3(1'b0), .out(multiplexer_5_out), .sel(OP));
  comparador_cero comparador_cero_1 (.A(B), .Z(comparador_cero_1_z));
  es1000 es1000_1 (.in_1(B), .out_2(es1000_1_out_2));
  xnor xnor_1 (xnor_1_out, comparador_cero_1_z, es1000_1_out_2);
  Hex_Digit_Display hex_digit_display_1 (.value(S));  // open: dp
  and and_1 (C, multiplexer_5_out, xnor_1_out);
endmodule

module verificador (
  output [3:0] out_1,
  output [3:0] out_2,
  output [1:0] out_3,
  output halt,
  output N,
  output Z,
  output V,
  output C,
  output [3:0] res
);

  wire clock_1_out;
  wire [3:0] alu_1_s;

  Clock clock_1 (.out(clock_1_out));
  Counter #(.max('h3ff), .width(10)) counter_1 (
    .clk(clock_1_out), .carry(halt), .Q({out_3, out_2, out_1}));  // open: clr, load, up, count, D
  ALU alu_1 (.A(out_1), .B(out_2), .OP(out_3), .N(N), .V(Z), .Z(V), .S(alu_1_s), .C(C));
endmodule

module ANDBitaBit (
  input  [3:0] A,
  input  [3:0] B,
  output Z,
  output [3:0] S,
  output N
);

  and and_1 (S[0], A[0], B[0]);
  and and_2 (S[1], A[1], B[1]);
  and and_3 (S[2], A[2], B[2]);
  and and_4 (N, A[3], B[3]);
  comparador_cero comparador_cero_1 (.A({N, S[2:0]}), .Z(Z));

  assign S[3] = N;
endmodule

module ORBitABit (
  input  [3:0] A,
  input  [3:0] B,
  output Z,
  output [3:0] S,
  output N
);

  or or_1 (S[0], A[0], B[0]);
  or or_2 (S[1], A[1], B[1]);
  or or_3 (S[2], A[2], B[2]);
  or or_4 (N, A[3], B[3]);
  comparador_cero comparador_cero_1 (.A({N, S[2:0]}), .Z(Z));

  assign S[3] = N;
endmodule

module es1000 (
  input  [3:0] in_1,
  output out_2
);

  wire nor_1_out, or_1_out;

  or or_1 (or_1_out, in_1[1], in_1[2]);
  nor nor_1 (nor_1_out, in_1[0], or_1_out);
  and and_1 (out_2, nor_1_out, in_1[3]);
endmodule
